# Fritzing sketch MultipleToggleSwtiches (saved by Fritzing 0.9.2b)
breadboards: 1

parts:
  Part1 = Arduino Uno (Rev3)
  S1 = Toggle Switch [package=THT]
  R3 = Resistor [tolerance=±20% resistance=10k package=THT]
  S2 = Toggle Switch [package=THT]
  R4 = Resistor [tolerance=±20% resistance=10k package=THT]
  S3 = Toggle Switch [package=THT]
  R5 = Resistor [tolerance=±20% resistance=10k package=THT]

nets:
  N1: Part1.D2, S1.COM
  N2: Part1.D3_PWM, S2.COM
  N3: Part1.D4, S3.COM
  N4: Part1.5V, S1.L2, S2.L2, S3.L2
  N5: Part1.GND, R3.Pin_0, R4.Pin_0, R5.Pin_0
  N6: S1.L1, R3.Pin_1
  N7: S2.L1, R4.Pin_1
  N8: S3.L1, R5.Pin_1
